# Fritzing sketch Untitled Sketch (saved by Fritzing 0.9.3b)

parts:
  Часть1 = Arduino Nano (Rev3.0)
  LCD1 = LCD screen
  LCM1602_IIC2 = LCM1602 IIC [part_number="LCM1602 IIC" chip_label="LCM1602 IIC" package="DIP (Dual Inline) [THT]"]
  RHT2 = Humidity and Temperature Sensor RHT03 [part_number=DHT22]
  Часть2 = Adafruit BMP180
  S1 = Pushbutton [package="[THT]"]
  Часть3 = Adafruit DS3231 [part_number="Adafruit #3013"]

nets:
  GND: Часть1.GND, LCM1602_IIC2.GND, RHT2.GND_2, Часть2.GND, S1.Pin_2, Часть3.GND
  N1: Часть1.D6, RHT2.Data-signal
  VCC: Часть1.5V, LCM1602_IIC2.VCC, RHT2.Vcc, Часть2.+5V, Часть3.Vin
  N2: Часть1.A5, LCM1602_IIC2.SCL, Часть2.SCL, Часть3.SCL
  N3: Часть1.A4, LCM1602_IIC2.SDA, Часть2.SDA, Часть3.SDA
  VSS: LCD1.VSS, LCM1602_IIC2.VSS
  VDD: LCD1.VDD, LCM1602_IIC2.VDD
  N4: LCD1.V0, LCM1602_IIC2.V0
  N5: LCD1.RS, LCM1602_IIC2.RS
  N6: LCD1.R/W, LCM1602_IIC2.RW
  N7: LCD1.E, LCM1602_IIC2.E
  N8: LCD1.DB0, LCM1602_IIC2.D0
  N9: LCD1.DB1, LCM1602_IIC2.D1
  N10: LCD1.DB2, LCM1602_IIC2.D2
  N11: LCD1.DB3, LCM1602_IIC2.D3
  N12: LCD1.DB4, LCM1602_IIC2.D4
  N13: LCD1.DB5, LCM1602_IIC2.D5
  N14: LCD1.DB6, LCM1602_IIC2.D6
  N15: LCD1.DB7, LCM1602_IIC2.D7
  N16: LCD1.LED+, LCM1602_IIC2.A
  N17: LCD1.LED-, LCM1602_IIC2.K
  N18: LCM1602_IIC2.LED_A, LCM1602_IIC2.LED_B

notes:
  A4 = SDA
  A5 = SCL

custom parts:
  LCM1602 IIC: I2C-Module to use a 1602 or 2004 LCD on with the wire.h libory Serial LCD Modul
  Adafruit BMP180: This precision sensor from Bosch is the best low-cost sensing solution for measuring barometric pressure and temperature. Because pressure changes with altitude you can also use it as an altimeter! The sensor is soldered onto a PCB with a 3.3V regulator, I2C level shifter and pull-up resistors on the I2C pins. The BMP180 is the next-generation of sensors from Bosch, and replaces the BMP085.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
  Adafruit DS3231: The datasheet for the DS3231 explains that this part is an "Extremely Accurate I²C-Integrated RTC/TCXO/Crystal". And, hey, it does exactly what it says on the tin! This Real Time Clock (RTC) is the most precise you can get in a small, low power package. Most RTCs use an external 32kHz timing crystal that is used to keep time with low current draw. And that's all well and good, but those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
